// Logisim project Adder1Bit.circ as structural Verilog: 1 circuit, main circuit Adder1Bit
module Adder1Bit (
  input  cin,
  input  a,
  input  b,
  output s,
  output cout
);

  wire and_1_out, and_2_out, xor_1_out;

  xor xor_1 (xor_1_out, a, b);
  xor xor_2 (s, xor_1_out, cin);
  and and_1 (and_1_out, xor_1_out, cin);
  and and_2 (and_2_out, a, b);
  or or_1 (cout, and_1_out, and_2_out);
endmodule
