// Logisim project Adder32Bit.circ as structural Verilog: 1 circuit, main circuit Adder32Bit
module Adder32Bit (
  input  [31:0] a,
  input  [31:0] b,
  output [31:0] s,
  output cout
);

  wire adder1bit_2_cout, adder1bit_3_cout, adder1bit_4_cout, adder1bit_5_cout, adder1bit_6_cout,
       adder1bit_7_cout, adder1bit_8_cout, adder1bit_9_cout, adder1bit_10_cout, adder1bit_11_cout,
       adder1bit_12_cout, adder1bit_13_cout, adder1bit_14_cout, adder1bit_15_cout, adder1bit_16_cout,
       adder1bit_17_cout, adder1bit_18_cout, adder1bit_19_cout, adder1bit_20_cout, adder1bit_21_cout,
       adder1bit_22_cout, adder1bit_23_cout, adder1bit_24_cout, adder1bit_25_cout, adder1bit_26_cout,
       adder1bit_27_cout, adder1bit_28_cout, adder1bit_29_cout, adder1bit_30_cout, adder1bit_31_cout,
       adder1bit_32_cout;

  Adder1Bit adder1bit_1 (.a(a[31]), .b(b[31]), .cin(adder1bit_2_cout), .cout(cout), .s(s[31]));
  Adder1Bit adder1bit_2 (.a(a[30]), .b(b[30]), .cin(adder1bit_3_cout), .cout(adder1bit_2_cout), .s(s[30]));
  Adder1Bit adder1bit_3 (.a(a[29]), .b(b[29]), .cin(adder1bit_4_cout), .cout(adder1bit_3_cout), .s(s[29]));
  Adder1Bit adder1bit_4 (.a(a[28]), .b(b[28]), .cin(adder1bit_5_cout), .cout(adder1bit_4_cout), .s(s[28]));
  Adder1Bit adder1bit_5 (.a(a[27]), .b(b[27]), .cin(adder1bit_7_cout), .cout(adder1bit_5_cout), .s(s[27]));
  Adder1Bit adder1bit_6 (.a(a[25]), .b(b[25]), .cin(adder1bit_9_cout), .cout(adder1bit_6_cout), .s(s[25]));
  Adder1Bit adder1bit_7 (.a(a[26]), .b(b[26]), .cin(adder1bit_6_cout), .cout(adder1bit_7_cout), .s(s[26]));
  Adder1Bit adder1bit_8 (.a(a[23]), .b(b[23]), .cin(adder1bit_10_cout), .cout(adder1bit_8_cout), .s(s[23]));
  Adder1Bit adder1bit_9 (.a(a[24]), .b(b[24]), .cin(adder1bit_8_cout), .cout(adder1bit_9_cout), .s(s[24]));
  Adder1Bit adder1bit_10 (.a(a[22]), .b(b[22]), .cin(adder1bit_11_cout), .cout(adder1bit_10_cout), .s(s[22]));
  Adder1Bit adder1bit_11 (.a(a[21]), .b(b[21]), .cin(adder1bit_13_cout), .cout(adder1bit_11_cout), .s(s[21]));
  Adder1Bit adder1bit_12 (.a(a[19]), .b(b[19]), .cin(adder1bit_15_cout), .cout(adder1bit_12_cout), .s(s[19]));
  Adder1Bit adder1bit_13 (.a(a[20]), .b(b[20]), .cin(adder1bit_12_cout), .cout(adder1bit_13_cout), .s(s[20]));
  Adder1Bit adder1bit_14 (.a(a[17]), .b(b[17]), .cin(adder1bit_17_cout), .cout(adder1bit_14_cout), .s(s[17]));
  Adder1Bit adder1bit_15 (.a(a[18]), .b(b[18]), .cin(adder1bit_14_cout), .cout(adder1bit_15_cout), .s(s[18]));
  Adder1Bit adder1bit_16 (.a(a[15]), .b(b[15]), .cin(adder1bit_19_cout), .cout(adder1bit_16_cout), .s(s[15]));
  Adder1Bit adder1bit_17 (.a(a[16]), .b(b[16]), .cin(adder1bit_16_cout), .cout(adder1bit_17_cout), .s(s[16]));
  Adder1Bit adder1bit_18 (.a(a[13]), .b(b[13]), .cin(adder1bit_21_cout), .cout(adder1bit_18_cout), .s(s[13]));
  Adder1Bit adder1bit_19 (.a(a[14]), .b(b[14]), .cin(adder1bit_18_cout), .cout(adder1bit_19_cout), .s(s[14]));
  Adder1Bit adder1bit_20 (.a(a[11]), .b(b[11]), .cin(adder1bit_23_cout), .cout(adder1bit_20_cout), .s(s[11]));
  Adder1Bit adder1bit_21 (.a(a[12]), .b(b[12]), .cin(adder1bit_20_cout), .cout(adder1bit_21_cout), .s(s[12]));
  Adder1Bit adder1bit_22 (.a(a[9]), .b(b[9]), .cin(adder1bit_25_cout), .cout(adder1bit_22_cout), .s(s[9]));
  Adder1Bit adder1bit_23 (.a(a[10]), .b(b[10]), .cin(adder1bit_22_cout), .cout(adder1bit_23_cout), .s(s[10]));
  Adder1Bit adder1bit_24 (.a(a[7]), .b(b[7]), .cin(adder1bit_27_cout), .cout(adder1bit_24_cout), .s(s[7]));
  Adder1Bit adder1bit_25 (.a(a[8]), .b(b[8]), .cin(adder1bit_24_cout), .cout(adder1bit_25_cout), .s(s[8]));
  Adder1Bit adder1bit_26 (.a(a[5]), .b(b[5]), .cin(adder1bit_28_cout), .cout(adder1bit_26_cout), .s(s[5]));
  Adder1Bit adder1bit_27 (.a(a[6]), .b(b[6]), .cin(adder1bit_26_cout), .cout(adder1bit_27_cout), .s(s[6]));
  Adder1Bit adder1bit_28 (.a(a[4]), .b(b[4]), .cin(adder1bit_29_cout), .cout(adder1bit_28_cout), .s(s[4]));
  Adder1Bit adder1bit_29 (.a(a[3]), .b(b[3]), .cin(adder1bit_30_cout), .cout(adder1bit_29_cout), .s(s[3]));
  Adder1Bit adder1bit_30 (.a(a[2]), .b(b[2]), .cin(adder1bit_31_cout), .cout(adder1bit_30_cout), .s(s[2]));
  Adder1Bit adder1bit_31 (.a(a[1]), .b(b[1]), .cin(adder1bit_32_cout), .cout(adder1bit_31_cout), .s(s[1]));
  Adder1Bit adder1bit_32 (.a(a[0]), .b(b[0]), .cin(1'b0), .cout(adder1bit_32_cout), .s(s[0]));
endmodule
