// Logisim project Shifter.circ as structural Verilog: 1 circuit, main circuit Shifter
module Shifter (
  input  cin,
  input  [31:0] i1,
  input  [31:0] i0,
  output [31:0] o1,
  output [31:0] o0,
  output cout
);


  assign cout = i0[0];
  assign o0 = {i1[0], i0[31:1]};
  assign o1 = {cin, i1[31:1]};
endmodule
