// Logisim project control.circ as structural Verilog: 1 circuit, main circuit control
module control (
  input  cr_eq,
  input  pr0,
  input  go,
  input  clk,
  output ms_l,
  output co_m,
  output co_l,
  output c_i,
  output c_r,
  output p1_m,
  output p1_l,
  output p0_m,
  output p0_l
);

  wire and_1_out, and_4_out, and_5_out, and_8_out, and_9_out;
  wire [2:0] or_1_out, register_1_q;

  Register #(.width(3)) register_1 (.D(or_1_out), .Q(register_1_q), .clk(clk));  // open: en, clr
  and and_1 (and_1_out, ~register_1_q[2], ~register_1_q[1], ~register_1_q[0], go);  // AND_Gate
  and and_2 (ms_l, ~register_1_q[2], ~register_1_q[1], register_1_q[0]);  // AND_Gate
  and and_3 (c_r, ~register_1_q[2], register_1_q[1], ~register_1_q[0]);  // AND_Gate
  and and_4 (and_4_out, ~register_1_q[2], register_1_q[1], register_1_q[0], pr0);  // AND_Gate
  and and_5 (and_5_out, ~register_1_q[2], register_1_q[1], register_1_q[0], ~pr0);  // AND_Gate
  and and_6 (co_m, register_1_q[2], ~register_1_q[1], ~register_1_q[0]);  // AND_Gate
  and and_7 (c_i, register_1_q[2], ~register_1_q[1], register_1_q[0]);  // AND_Gate
  and and_8 (and_8_out, register_1_q[2], register_1_q[1], ~register_1_q[0], ~cr_eq);  // AND_Gate
  and and_9 (and_9_out, register_1_q[2], register_1_q[1], ~register_1_q[0], cr_eq);  // AND_Gate
  or or_1 (or_1_out[0], and_9_out, and_8_out, co_m, and_5_out, c_r, and_1_out);
  or or_2 (or_1_out[1], and_9_out, and_8_out, c_i, c_r, ms_l);
  or or_3 (or_1_out[2], and_9_out, c_i, co_m, and_5_out, and_4_out);
  or or_4 (co_l, and_4_out, and_5_out, co_m);
  or or_5 (p1_l, co_m, c_i);
  or or_6 (p0_l, c_r, c_i);

  assign p0_m = c_r;
  assign p1_m = co_m;
endmodule
