// Logisim project datapath.circ as structural Verilog: 4 circuits, main circuit datapath
module datapath (
  input  [31:0] Multiplier,
  input  [31:0] Multiplicand,
  input  ms_l,
  input  co_m,
  input  co_l,
  input  c_i,
  input  c_r,
  input  p1_m,
  input  p1_l,
  input  p0_m,
  input  p0_l,
  input  clk,
  output cr_eq,
  output pr0,
  output [31:0] Product1,
  output [31:0] Product0
);

  wire adder32_bit_1_cout, Cout_q, multiplexer_1_out;
  wire [5:0] Counter_q;
  wire [31:0] adder32_bit_1_s, multiplexer_2_out, multiplexer_3_out, Multiplicand_q, Multiplier_q,
       shifter64_bit_1_o0, shifter64_bit_1_o1;

  Register #(.width(32)) u_Multiplier (.D(Multiplier), .en(ms_l), .Q(Multiplier_q), .clk(clk));  // open: clr
  Register #(.width(32)) u_Multiplicand (.D(Multiplicand), .en(ms_l), .Q(Multiplicand_q), .clk(clk));  // open: clr
  Multiplexer #(.enable("false")) multiplexer_1 (
    .in0(1'b0), .in1(adder32_bit_1_cout), .out(multiplexer_1_out), .sel(co_m));
  Register #(.width(1)) Cout (.D(multiplexer_1_out), .en(co_l), .Q(Cout_q), .clk(clk));  // open: clr
  Counter #(.width(6), .max('h20)) Counter (.count(c_i), .Q(Counter_q), .clk(clk), .clr(c_r));  // open: load, D, carry
  Multiplexer #(.width(32), .enable("false")) multiplexer_2 (
    .in0(shifter64_bit_1_o1), .in1(adder32_bit_1_s), .out(multiplexer_2_out), .sel(p1_m));
  Register #(.width(32)) u_Product1 (.D(multiplexer_2_out), .en(p1_l), .Q(Product1), .clk(clk));  // open: clr
  Multiplexer #(.width(32), .enable("false")) multiplexer_3 (
    .in0(shifter64_bit_1_o0), .in1(Multiplier_q), .out(multiplexer_3_out), .sel(p0_m));
  Register #(.width(32)) u_Product0 (.D(multiplexer_3_out), .en(p0_l), .Q(Product0), .clk(clk));  // open: clr
  Adder32_bit adder32_bit_1 (.a(Product1), .b(Multiplicand_q), .s(adder32_bit_1_s), .cout(adder32_bit_1_cout));
  Comparator #(.width(6), .mode("unsigned")) comparator_1 (.a(6'b100000), .b(Counter_q), .eq(cr_eq));  // open: gt, lt
  Shifter64_bit shifter64_bit_1 (
    .cin(Cout_q), .i1(Product1), .i0(Product0), .o1(shifter64_bit_1_o1), .o0(shifter64_bit_1_o0), .cout(pr0));
endmodule

module Adder1bit (
  input  b,
  input  a,
  input  cin,
  output cout,
  output s
);

  wire and_1_out, and_2_out, xor_1_out;

  xor xor_1 (xor_1_out, a, b);
  xor xor_2 (s, xor_1_out, cin);
  and and_1 (and_1_out, xor_1_out, cin);
  or or_1 (cout, and_1_out, and_2_out);
  and and_2 (and_2_out, a, b);
endmodule

module Adder32_bit (
  input  [31:0] a,
  input  [31:0] b,
  output [31:0] s,
  output cout
);

  wire adder1bit_2_cout, adder1bit_3_cout, adder1bit_4_cout, adder1bit_5_cout, adder1bit_6_cout,
       adder1bit_7_cout, adder1bit_8_cout, adder1bit_9_cout, adder1bit_10_cout, adder1bit_11_cout,
       adder1bit_12_cout, adder1bit_13_cout, adder1bit_14_cout, adder1bit_15_cout, adder1bit_16_cout,
       adder1bit_17_cout, adder1bit_18_cout, adder1bit_19_cout, adder1bit_20_cout, adder1bit_21_cout,
       adder1bit_22_cout, adder1bit_23_cout, adder1bit_24_cout, adder1bit_25_cout, adder1bit_26_cout,
       adder1bit_27_cout, adder1bit_28_cout, adder1bit_29_cout, adder1bit_30_cout, adder1bit_31_cout,
       adder1bit_32_cout;

  Adder1bit adder1bit_1 (.cout(cout), .b(b[31]), .a(a[31]), .s(s[31]), .cin(adder1bit_3_cout));
  Adder1bit adder1bit_2 (.cout(adder1bit_2_cout), .b(b[29]), .a(a[29]), .s(s[29]), .cin(adder1bit_4_cout));
  Adder1bit adder1bit_3 (.cout(adder1bit_3_cout), .b(b[30]), .a(a[30]), .s(s[30]), .cin(adder1bit_2_cout));
  Adder1bit adder1bit_4 (.cout(adder1bit_4_cout), .b(b[28]), .a(a[28]), .s(s[28]), .cin(adder1bit_5_cout));
  Adder1bit adder1bit_5 (.cout(adder1bit_5_cout), .b(b[27]), .a(a[27]), .s(s[27]), .cin(adder1bit_6_cout));
  Adder1bit adder1bit_6 (.cout(adder1bit_6_cout), .b(b[26]), .a(a[26]), .s(s[26]), .cin(adder1bit_7_cout));
  Adder1bit adder1bit_7 (.cout(adder1bit_7_cout), .b(b[25]), .a(a[25]), .s(s[25]), .cin(adder1bit_8_cout));
  Adder1bit adder1bit_8 (.cout(adder1bit_8_cout), .b(b[24]), .a(a[24]), .s(s[24]), .cin(adder1bit_9_cout));
  Adder1bit adder1bit_9 (.cout(adder1bit_9_cout), .b(b[23]), .a(a[23]), .s(s[23]), .cin(adder1bit_10_cout));
  Adder1bit adder1bit_10 (.cout(adder1bit_10_cout), .b(b[22]), .a(a[22]), .s(s[22]), .cin(adder1bit_11_cout));
  Adder1bit adder1bit_11 (.cout(adder1bit_11_cout), .b(b[21]), .a(a[21]), .s(s[21]), .cin(adder1bit_12_cout));
  Adder1bit adder1bit_12 (.cout(adder1bit_12_cout), .b(b[20]), .a(a[20]), .s(s[20]), .cin(adder1bit_13_cout));
  Adder1bit adder1bit_13 (.cout(adder1bit_13_cout), .b(b[19]), .a(a[19]), .s(s[19]), .cin(adder1bit_14_cout));
  Adder1bit adder1bit_14 (.cout(adder1bit_14_cout), .b(b[18]), .a(a[18]), .s(s[18]), .cin(adder1bit_15_cout));
  Adder1bit adder1bit_15 (.cout(adder1bit_15_cout), .b(b[17]), .a(a[17]), .s(s[17]), .cin(adder1bit_17_cout));
  Adder1bit adder1bit_16 (.cout(adder1bit_16_cout), .b(b[15]), .a(a[15]), .s(s[15]), .cin(adder1bit_18_cout));
  Adder1bit adder1bit_17 (.cout(adder1bit_17_cout), .b(b[16]), .a(a[16]), .s(s[16]), .cin(adder1bit_16_cout));
  Adder1bit adder1bit_18 (.cout(adder1bit_18_cout), .b(b[14]), .a(a[14]), .s(s[14]), .cin(adder1bit_19_cout));
  Adder1bit adder1bit_19 (.cout(adder1bit_19_cout), .b(b[13]), .a(a[13]), .s(s[13]), .cin(adder1bit_20_cout));
  Adder1bit adder1bit_20 (.cout(adder1bit_20_cout), .b(b[12]), .a(a[12]), .s(s[12]), .cin(adder1bit_21_cout));
  Adder1bit adder1bit_21 (.cout(adder1bit_21_cout), .b(b[11]), .a(a[11]), .s(s[11]), .cin(adder1bit_22_cout));
  Adder1bit adder1bit_22 (.cout(adder1bit_22_cout), .b(b[10]), .a(a[10]), .s(s[10]), .cin(adder1bit_23_cout));
  Adder1bit adder1bit_23 (.cout(adder1bit_23_cout), .b(b[9]), .a(a[9]), .s(s[9]), .cin(adder1bit_24_cout));
  Adder1bit adder1bit_24 (.cout(adder1bit_24_cout), .b(b[8]), .a(a[8]), .s(s[8]), .cin(adder1bit_25_cout));
  Adder1bit adder1bit_25 (.cout(adder1bit_25_cout), .b(b[7]), .a(a[7]), .s(s[7]), .cin(adder1bit_27_cout));
  Adder1bit adder1bit_26 (.cout(adder1bit_26_cout), .b(b[5]), .a(a[5]), .s(s[5]), .cin(adder1bit_29_cout));
  Adder1bit adder1bit_27 (.cout(adder1bit_27_cout), .b(b[6]), .a(a[6]), .s(s[6]), .cin(adder1bit_26_cout));
  Adder1bit adder1bit_28 (.cout(adder1bit_28_cout), .b(b[3]), .a(a[3]), .s(s[3]), .cin(adder1bit_30_cout));
  Adder1bit adder1bit_29 (.cout(adder1bit_29_cout), .b(b[4]), .a(a[4]), .s(s[4]), .cin(adder1bit_28_cout));
  Adder1bit adder1bit_30 (.cout(adder1bit_30_cout), .b(b[2]), .a(a[2]), .s(s[2]), .cin(adder1bit_31_cout));
  Adder1bit adder1bit_31 (.cout(adder1bit_31_cout), .b(b[1]), .a(a[1]), .s(s[1]), .cin(adder1bit_32_cout));
  Adder1bit adder1bit_32 (.cout(adder1bit_32_cout), .b(b[0]), .a(a[0]), .s(s[0]), .cin(1'b0));
endmodule

module Shifter64_bit (
  input  cin,
  input  [31:0] i1,
  input  [31:0] i0,
  output [31:0] o1,
  output [31:0] o0,
  output cout
);


  assign cout = i0[0];
  assign o0 = {i1[0], i0[31:1]};
  assign o1 = {cin, i1[31:1]};
endmodule
