// Logisim project mult32.circ as structural Verilog: 1 circuit, main circuit mult32
module mult32 (
  input  [31:0] in_1,
  input  [31:0] in_2,
  output [31:0] out_3,
  output [31:0] out_4
);

  wire button_1_out, clock_1_out, control_1_c_i, control_1_c_r, control_1_co_l, control_1_co_m,
       control_1_ms_l, control_1_p0_l, control_1_p0_m, control_1_p1_l, control_1_p1_m, datapath_1_cr_eq,
       datapath_1_pr0;

  Button button_1 (.out(button_1_out));
  Clock clock_1 (.out(clock_1_out));
  control control_1 (
    .cr_eq(datapath_1_cr_eq), .pr0(datapath_1_pr0), .go(button_1_out), .clk(clock_1_out),
    .ms_l(control_1_ms_l), .co_m(control_1_co_m), .co_l(control_1_co_l), .c_i(control_1_c_i),
    .c_r(control_1_c_r), .p1_m(control_1_p1_m), .p1_l(control_1_p1_l), .p0_m(control_1_p0_m),
    .p0_l(control_1_p0_l));
  datapath datapath_1 (
    .Multiplier(in_1), .Multiplicand(in_2), .ms_l(control_1_ms_l), .co_m(control_1_co_m),
    .co_l(control_1_co_l), .c_i(control_1_c_i), .c_r(control_1_c_r), .p1_m(control_1_p1_m),
    .p1_l(control_1_p1_l), .p0_m(control_1_p0_m), .p0_l(control_1_p0_l), .clk(clock_1_out),
    .cr_eq(datapath_1_cr_eq), .pr0(datapath_1_pr0), .Product1(out_3), .Product0(out_4));
endmodule
